# Fritzing sketch Untitled Sketch (saved by Fritzing 0.9.4)
breadboards: 1

parts:
  Part1 = Arduino Uno (Rev3) - ICSP
  U1 = LCD-16X2 [package=lcd-16x2_noholes]
  RHT1 = Humidity and Temperature Sensor RHT03
  YL-83_-_Control_Board1 = YL-83 Rain Sensor - Control Board
  YL-83_-_Detection_Board1 = YL-83 Rain Sensor - Detection Board
  Part2 = FC-28 Soil Hygrometer Module
  Part3 = FC-28 Soil Hygrometer Module - Probe
  U2 = POT [package=pot_mammoth]
  J1 = Piezo Speaker
  LED1 = smd LED [color="Red (633nm)" package="1206 [SMD]"]
  LED2 = smd LED [color="Yellow (595nm)" package="1206 [SMD]"]
  LED3 = smd LED [color="Green (565nm)" package="1206 [SMD]"]
  R1 = Resistor [tolerance=±5% resistance=4.7k package=THT]

nets:
  N1: Part1.A0, YL-83_-_Control_Board1.AO
  N2: Part1.A1, Part2.AO
  N3: Part1.ICSP_MOSI, Part1.D11_PWM/MOSI, LED1.anode
  N4: Part1.D8, RHT1.Vcc
  N5: Part1.D9_PWM, YL-83_-_Control_Board1.DO
  N6: Part1.D10_PWM/SS, J1.pin2
  N7: Part1.D12/MISO, LED2.anode
  N8: Part1.D13/SCK, LED3.anode
  N9: Part1.D2, U1.DB7
  N10: Part1.D3_PWM, U1.DB6
  N11: Part1.D4, U1.DB5
  N12: Part1.D5_PWM, U1.DB4
  N13: Part1.D6_PWM, U1.E
  N14: Part1.D7, U1.RS
  VCC: Part1.5V, U1.VDD, RHT1.Data-signal, YL-83_-_Control_Board1.VCC, Part2.VCC, U2.E, R1.Pin_1
  GND: Part1.GND, U1.VSS, U1.R_W, U1.K, RHT1.GND_1, YL-83_-_Control_Board1.GND, Part2.GND, U2.S, J1.pin1, LED1.cathode, LED2.cathode, LED3.cathode
  N15: U1.VO, U2.A
  N16: U1.A, R1.Pin_0
  N17: YL-83_-_Control_Board1.POS, YL-83_-_Detection_Board1.POS
  N18: YL-83_-_Control_Board1.NEG, YL-83_-_Detection_Board1.NEG
  N19: Part2.POS, Part3.POS
  N20: Part2.NEG, Part3.NEG

custom parts:
  YL-83 Rain Sensor - Control Board: The YL-83 is a rain sensor that has more resistance when dry and less resistance when wet. The module runs at 5V.
  YL-83 Rain Sensor - Detection Board: The YL-83 is a rain sensor that has more resistance when dry and less resistance when wet. The module runs at 5V.
  FC-28 Soil Hygrometer Module: The FC-28 is a soil hygrometer module that uses the Texas Instruments LM393 comparator chip to provide an analog measurement of soil humidity. The digital output is high when soil moisture is over a certain threshold, as determined by adjusting the potentiometer.
  FC-28 Soil Hygrometer Module - Probe: The FC-28 is a soil hygrometer module that uses the Texas Instruments LM393 comparator chip to provide an analog measurement of soil humidity.

// code stored in the sketch: Untitled2.ino
#include <LiquidCrystal.h>
#include "DHT.h"
 
#define DHTPIN 8          
 
LiquidCrystal lcd(7, 6, 5, 4, 3, 2);
 
#define DHTTYPE DHT22       
DHT dht(DHTPIN, DHTTYPE);   
 
char temperature[] = "Temp = 00.0 C";
char humidity[]    = "Vlaz = 00.0 %";
const int hummidityd = 9;
const int hummiditya = A0;
const int buzzer = 10;
const int hygrometer = A1;
int led1=13;
int led2=12;
int led3=11;
int value_analog;
int value;

void setup() {
  Serial.begin(9600);
  lcd.begin(16, 2);
  dht.begin();
  pinMode(hummidityd, INPUT);
  pinMode(hummidityd, INPUT);
  pinMode (buzzer, OUTPUT);
  pinMode (led1, OUTPUT);
  pinMode (led2, OUTPUT);
  pinMode (led3, OUTPUT);
}
 
void loop() {
  delay(1000);               
  int Vlaz = dht.readHumidity() * 10;
  int Temp = dht.readTemperature() * 10;
  if (isnan(Vlaz) || isnan(Temp)) {
    lcd.clear();
    lcd.setCursor(5, 0);
    lcd.print("Error");
    return;
  }
  if(Temp < 0){
    temperature[6] = '-';
    Temp = abs(Temp);
  }
  else
  temperature[6] = ' ';
  temperature[7]   = (Temp / 100)%10  + 48;
  temperature[8]   = (Temp / 10)  % 10  + 48;
  temperature[10]  =  Temp % 10 + 48;
  temperature[11]  = 223;        
  if(Vlaz >= 1000)
    humidity[6]    = '1';
  else
  humidity[6]    = ' ';
  humidity[7]      = (Vlaz / 100) % 10 + 48;
  humidity[8]      = (Vlaz / 10) % 10 + 48;
  humidity[10]     =  Vlaz % 10 + 48;
  lcd.setCursor(0, 0);//Postavuvanje na pocetokot na pecatenjeto
  lcd.print(temperature);//pecatanje na temparaturata na LCD-to
  lcd.setCursor(0, 1);//Postavuvanje na pocetokot na pecatenjeto
  lcd.print(humidity);//Pecatenje na vlaznosta na LCD-to
  if(digitalRead(hummidityd) == LOW) 
  {
    Serial.println("Digital value : wet"); 
    delay(10);
    lcd.clear();
    lcd.setCursor(5, 0);
    lcd.print ("Zavrna");//Predupreduvanje deka zavrnalo na LCD ekran.
  }
else
  {
    Serial.println("Digital value : dry");
    delay(10); 
  }
value_analog=analogRead(hummidityd); 
 Serial.print("Analog value : ");
 Serial.println(value_analog); 
 Serial.println("");
  delay(1000);
   if(digitalRead(hummidityd) == LOW) 
  {
    tone(buzzer, 1000); 
    delay(1000); 
  }
else
  {
    noTone(buzzer);
    delay(1000); 
  }
    value = analogRead(hygrometer);    
  value = constrain(value,400,1023);  
  value = map(value,400,1023,100,0);  
  Serial.print("Vlaznost na pocvata: ");
  Serial.print(value);
  Serial.println("%");
  delay(2000); 
  if(value<=25)
  {
    digitalWrite(led1, HIGH);
  }
  else
  {
    digitalWrite(led1, LOW);
  }
  if(value>25 && value<75)
  {
    digitalWrite(led2, HIGH);
  }
  
  else
  {
    digitalWrite(led2, LOW);
  }
  if(value>=75)
  {
    digitalWrite(led3, HIGH);
    lcd.clear();
    lcd.print("Vlaznosta na pocvata e nad 75%");//Predupreduvanje deka vlaznosta na pocvata e nad 75% na LCD ekran.
  } 
  
  else
  {
    digitalWrite(led3, LOW);
  }
  }
